# Fritzing sketch Untitled Sketch 3 (saved by Fritzing 0.9.3b)
breadboards: 1

parts:
  Part1 = Arduino Ethernet Shield (Rev3)
  Part2 = Arduino Uno (Rev3) - ICSP  # not connected
  U1 = GAS_SENSOR [package=mq-3]
  J1 = Piezo Speaker
  GSM_SIM_GPSR_SMS_SIM900_SIM1 = SIM800L [package=THT]

nets:
  N1: Part1.PWM_D9, GSM_SIM_GPSR_SMS_SIM900_SIM1.SIM_TXD
  N2: Part1.ETH_CS, GSM_SIM_GPSR_SMS_SIM900_SIM1.SIM_RXD
  GND: Part1.GND, U1.A1, J1.pin1, GSM_SIM_GPSR_SMS_SIM900_SIM1.GND
  N3: Part1.A0, U1.B1
  N4: Part1.PWM_D3, J1.pin2
  N5: U1.H1, U1.H2

notes:
  <--- Ethernet Shield
  <---Arduino UNO
  Use MQ2 sensor
  Stack the ethernet shield on the arduino board, then make the connections on the shield
  <---GSM Module

// code stored in the sketch: Untitled2.ino
#include <SPI.h>
#include <Dhcp.h>
#include <Dns.h>
#include <Ethernet.h>
#include <EthernetClient.h>
#include <Temboo.h>
#define TEMBOO_ACCOUNT "iotarduino-asmitav"  // Your Temboo account name 
#define TEMBOO_APP_KEY_NAME "myFirstApp"  // Your Temboo app key name
#define TEMBOO_APP_KEY "SxJHOcBO6deBEqXivk3TRaSvNG3lIlPx"  // Your Temboo app key

#define ETHERNET_SHIELD_MAC {0xC0, 0x26, 0x1B, 0x5A, 0x70, 0x26}

const int gasPin=A0;
const int buzz=3;

byte ethernetMACAddress[] = ETHERNET_SHIELD_MAC;
EthernetClient client;

int numRuns = 1;   // Execution count, so this doesn't run forever
int maxRuns = 10;   // Maximum number of times the Choreo should be executed

// ThingSpeak Settings
char thingSpeakAddress[] = "api.thingspeak.com";
String writeAPIKey = "KE099C98QMLUZR0G";
const int updateThingSpeakInterval = 10 * 1000;      // Time interval in milliseconds to update ThingSpeak (number of seconds * 1000 = interval)

// Variable Setup
long lastConnectionTime = 0; 
boolean lastConnected = false;
int failedCounter = 0;

void setup() {
  // put your setup code here, to run once:
  pinMode(buzz,OUTPUT);
  // Start Serial for debugging on the Serial Monitor
  Serial.begin(9600);
  // Start Ethernet on Arduino
  startEthernet();

}

void loop() {
  // put your main code here, to run repeatedly:
  updateCloud();
  //Serial.println(analogRead(gasPin));
  //delay(1000);
  if(analogRead(gasPin)>250)
  {
    analogWrite(buzz,HIGH);
    sendEmail();
  }
  else
  {
    digitalWrite(buzz,LOW);
  }
}

void updateCloud()
{
  // Read value from Analog Input Pin 0
  String analogValue0 = String(analogRead(A0), DEC);
  
  // Print Update Response to Serial Monitor
  if (client.available())
  {
    char c = client.read();
    Serial.print(c);
  }

  // Disconnect from ThingSpeak
  if (!client.connected() && lastConnected)
  {
    Serial.println("...disconnected");
    Serial.println();
    
    client.stop();
  }
  
  // Update ThingSpeak
  if(!client.connected() && (millis() - lastConnectionTime > updateThingSpeakInterval))
  {
    updateThingSpeak("field1="+analogValue0);
  }
  
  // Check if Arduino Ethernet needs to be restarted
  if (failedCounter > 3 ) {startEthernet();}
  
  lastConnected = client.connected();
}

void updateThingSpeak(String tsData)
{
  if (client.connect(thingSpeakAddress, 80))
  {         
    client.print("POST /update HTTP/1.1\n");
    client.print("Host: api.thingspeak.com\n");
    client.print("Connection: close\n");
    client.print("X-THINGSPEAKAPIKEY: "+writeAPIKey+"\n");
    client.print("Content-Type: application/x-www-form-urlencoded\n");
    client.print("Content-Length: ");
    client.print(tsData.length());
    client.print("\n\n");

    client.print(tsData);
    
    lastConnectionTime = millis();
    
    if (client.connected())
    {
      Serial.println("Connecting to ThingSpeak...");
      Serial.println();
      
      failedCounter = 0;
    }
    else
    {
      failedCounter++;
  
      Serial.println("Connection to ThingSpeak failed ("+String(failedCounter, DEC)+")");   
      Serial.println();
    }
    
  }
  else
  {
    failedCounter++;
    
    Serial.println("Connection to ThingSpeak Failed ("+String(failedCounter, DEC)+")");   
    Serial.println();
    
    lastConnectionTime = millis(); 
  }
}

void startEthernet()
{
  
  client.stop();

  Serial.println("Connecting Arduino to network...");
  Serial.println();  

  delay(1000);
  
  // Connect to network amd obtain an IP address using DHCP
  if (Ethernet.begin(ethernetMACAddress) == 0)
  {
    Serial.println("DHCP Failed, reset Arduino to try again");
    Serial.println();
  }
  else
  {
    Serial.println("Arduino connected to network using DHCP");
    Serial.println();
  }
  
  delay(1000);
}

void sendEmail()
{
  Serial.begin(9600);
  
  // For debugging, wait until the serial console is connected
  delay(4000);
  while(!Serial);

  Serial.print("DHCP:");
  if (Ethernet.begin(ethernetMACAddress) == 0) {
    Serial.println("FAIL");
    while(true);
  }
  Serial.println("OK");
  delay(5000);

  Serial.println("Setup complete.\n");
  
   if (numRuns <= maxRuns) {
    Serial.println("Running SendEmail - Run #" + String(numRuns++));

    TembooChoreo SendEmailChoreo(client);

    // Invoke the Temboo client
    SendEmailChoreo.begin();

    // Set Temboo account credentials
    SendEmailChoreo.setAccountName(TEMBOO_ACCOUNT);
    SendEmailChoreo.setAppKeyName(TEMBOO_APP_KEY_NAME);
    SendEmailChoreo.setAppKey(TEMBOO_APP_KEY);

    // Set Choreo inputs
    String FromAddressValue = "iotarduino-AsmitaV@temboo.com";
    SendEmailChoreo.addInput("FromAddress", FromAddressValue);
    String UsernameValue = "iotarduino.av@gmail.com";
    SendEmailChoreo.addInput("Username", UsernameValue);
    String SubjectValue = "Test-Successful";
    SendEmailChoreo.addInput("Subject", SubjectValue);
    String ToAddressValue = "asmita.v.1996@gmail.com";
    SendEmailChoreo.addInput("ToAddress", ToAddressValue);
    String PasswordValue = "krjrhcvgwbtwneox";
    SendEmailChoreo.addInput("Password", PasswordValue);
    String MessageBodyValue = "Sending from arduino uno";
    SendEmailChoreo.addInput("MessageBody", MessageBodyValue);

    // Identify the Choreo to run
    SendEmailChoreo.setChoreo("/Library/Google/Gmail/SendEmail");

    // Run the Choreo; when results are available, print them to serial
    SendEmailChoreo.run();

    while(SendEmailChoreo.available()) {
      char c = SendEmailChoreo.read();
      Serial.print(c);
    }
    SendEmailChoreo.close();
  }

  Serial.println("\nWaiting...\n");
  delay(30000); // wait 30 seconds between SendEmail calls
}
